// Logisim project mata3820171.circ as structural Verilog: 1 circuit, main circuit main
module main (
  input  [7:0] E3,
  input  [7:0] E2,
  input  [7:0] E1,
  input  [7:0] E0,
  input  [7:0] Entrada,
  input  [1:0] in_6,
  input  [1:0] in_7,
  input  in_8,
  input  [7:0] in_9,
  input  [7:0] in_10,
  output [7:0] out_11,
  output [7:0] out_12,
  output [7:0] out_13,
  output [7:0] out_14,
  output [1:0] out_15,
  output [1:0] out_16,
  output [7:0] out_17,
  output [7:0] out_18,
  output [7:0] out_19,
  output [7:0] out_20,
  output [7:0] out_21,
  output [7:0] out_22,
  output [7:0] out_23,
  output [7:0] out_24,
  output [7:0] out_25,
  output [7:0] out_26,
  output [7:0] out_27,
  output [7:0] out_28,
  output [7:0] out_29,
  output [3:0] out_30,
  output [7:0] out_31,
  output [7:0] out_32,
  output [7:0] out_33,
  output [7:0] out_34,
  output [7:0] out_35,
  output [7:0] out_36,
  output [7:0] out_37,
  output [7:0] out_38,
  output [7:0] out_39,
  output [7:0] out_40,
  output [7:0] out_41,
  output [7:0] out_42,
  output [7:0] out_43,
  output [7:0] out_44,
  output [7:0] out_45,
  output [7:0] out_46,
  output [7:0] out_47,
  output [7:0] out_48,
  output [7:0] out_49,
  output [7:0] out_50,
  output [7:0] out_51
);

  wire adder_1_cout, clock_1_out, comparator_1_eq, comparator_2_lt, comparator_3_gt, comparator_4_eq,
       comparator_4_lt, comparator_5_eq, comparator_5_gt, or_1_out, or_2_out, undriven;
  wire [7:0] multiplexer_1_out, multiplexer_2_out, multiplexer_8_out;

  BitSelector #(.group(4)) bitselector_1 (.in(Entrada), .out(out_30), .sel(in_8));
  BitSelector #(.group(2)) bitselector_2 (.in(Entrada), .out(out_16), .sel(in_7));
  BitSelector #(.group(2)) bitselector_3 (.in(Entrada), .out(out_15), .sel(in_6));
  Clock clock_1 (.out(clock_1_out));
  Multiplexer #(.select(2), .width(8)) multiplexer_1 (
    .in0(out_14), .in1(out_13), .in2(out_12), .in3(out_11), .out(multiplexer_1_out), .sel(out_15));  // open: en
  Register R0 (.D(multiplexer_8_out), .en(undriven), .Q(out_14), .clk(clock_1_out));  // open: clr
  Register R1 (.D(E1), .Q(out_13), .clk(clock_1_out));  // open: en, clr
  Register R3 (.D(E3), .Q(out_11), .clk(clock_1_out));  // open: en, clr
  Register R2 (.D(E2), .Q(out_12), .clk(clock_1_out));  // open: en, clr
  Multiplexer #(.select(2), .width(8)) multiplexer_2 (
    .in0(out_14), .in1(out_13), .in2(out_12), .in3(out_11), .out(multiplexer_2_out), .sel(out_16));  // open: en
  Demultiplexer #(.select(4), .width(8)) demultiplexer_1 (
    .out0(out_18), .out1(out_19), .out2(out_21), .out3(out_22), .out4(out_23), .out5(out_25), .out6(out_26),
    .out7(out_28), .out8(out_29), .out9(out_31), .out10(out_33), .out11(out_34), .in(multiplexer_1_out),
    .sel(out_30));  // open: out12, out13, out14, out15, en
  Demultiplexer #(.select(4), .width(8)) demultiplexer_2 (
    .out0(out_37), .out1(out_39), .out2(out_40), .out3(out_41), .out4(out_42), .out5(out_43), .out6(out_45),
    .out7(out_46), .out8(out_47), .out9(out_48), .out10(out_49), .in(multiplexer_2_out), .sel(out_30));  // open: out11, out12, out13, out14, out15, en
  Comparator #(.mode("unsigned")) comparator_1 (.a(out_26), .b(out_45), .eq(comparator_1_eq));  // open: gt, lt
  Comparator #(.mode("unsigned")) comparator_2 (.a(out_28), .b(out_46), .lt(comparator_2_lt));  // open: gt, eq
  Comparator #(.mode("unsigned")) comparator_3 (.a(out_29), .b(out_47), .gt(comparator_3_gt));  // open: eq, lt
  Comparator #(.mode("unsigned")) comparator_4 (
    .a(out_31), .b(out_48), .eq(comparator_4_eq), .lt(comparator_4_lt));  // open: gt
  Comparator #(.mode("unsigned")) comparator_5 (
    .a(out_33), .b(out_49), .gt(comparator_5_gt), .eq(comparator_5_eq));  // open: lt
  or or_1 (or_1_out, comparator_4_eq, comparator_4_lt);
  or or_2 (or_2_out, comparator_5_gt, comparator_5_eq);
  assign out_17 = out_19 & out_37;  // AND_Gate and_1, 8 bits wide
  assign out_20 = out_18 | out_39;  // OR_Gate or_3, 8 bits wide
  assign out_24 = out_21 ^ out_40;  // XOR_Gate xor_1, 8 bits wide
  assign out_27 = ~out_22;  // NOT_Gate not_1, 8 bits wide
  Adder adder_1 (.a(out_23), .b(out_42), .out(out_32), .cout(adder_1_cout));  // open: cin
  Subtractor subtractor_1 (.a(out_25), .b(out_43), .out(out_35));  // open: bin, bout
  Multiplexer #(.width(8)) multiplexer_3 (.in0(in_9), .in1(in_10), .out(out_36), .sel(comparator_1_eq));  // open: en
  Multiplexer #(.width(8)) multiplexer_4 (.in0(in_9), .in1(in_10), .out(out_38), .sel(comparator_2_lt));  // open: en
  Multiplexer #(.width(8)) multiplexer_5 (.in0(in_9), .in1(in_10), .out(out_44), .sel(comparator_3_gt));  // open: en
  Multiplexer #(.width(8)) multiplexer_6 (.in0(in_9), .in1(in_10), .out(out_50), .sel(or_1_out));  // open: en
  Multiplexer #(.width(8)) multiplexer_7 (.in0(in_9), .in1(in_10), .out(out_51), .sel(or_2_out));  // open: en
  Multiplexer #(.select(4), .width(8)) multiplexer_8 (
    .in0(out_17), .in1(out_20), .in2(out_24), .in3(out_27), .in4(out_32), .in5(out_35), .in6(out_36),
    .in7(out_38), .in8(out_44), .in9(out_50), .in10(out_51), .out(multiplexer_8_out), .sel(out_30));  // open: in11, in12, in13, in14, in15, en

  // Notes on the sheet:
  //   Rx
  //   Ry
  //   Rx
  //   Ry
endmodule
