// Logisim project mata3820172.circ as structural Verilog: 1 circuit, main circuit main
module main (
  input  [7:0] E3,
  input  [7:0] E2,
  input  [7:0] E1,
  input  [7:0] E0,
  input  in_5,
  output [7:0] out_6,
  output [7:0] out_7,
  output [7:0] out_8,
  output [7:0] out_9,
  output [1:0] out_10,
  output [1:0] out_11,
  output [7:0] out_12,
  output [7:0] out_13,
  output [7:0] out_14,
  output [7:0] out_15,
  output [7:0] out_16,
  output [7:0] out_17,
  output [7:0] out_18,
  output [7:0] out_19,
  output [7:0] out_20,
  output [7:0] out_21,
  output [7:0] out_22,
  output [7:0] out_23,
  output [7:0] out_24,
  output [7:0] out_25,
  output [7:0] out_26,
  output [7:0] out_27,
  output [7:0] out_28,
  output [7:0] out_29,
  output [3:0] out_30,
  output [7:0] out_31,
  output [7:0] out_32,
  output [7:0] out_33,
  output [7:0] out_34,
  output [7:0] out_35,
  output [7:0] out_36,
  output [7:0] out_37,
  output [7:0] out_38,
  output [7:0] out_39,
  output [7:0] out_40,
  output [7:0] out_41,
  output [7:0] out_42,
  output [7:0] out_43,
  output [7:0] out_44,
  output [7:0] out_45,
  output [7:0] out_46
);

  wire adder_1_cout, clock_1_out, clock_2_out, comparator_1_eq, comparator_2_lt, comparator_3_gt,
       comparator_4_eq, comparator_4_lt, comparator_5_eq, comparator_5_gt, not_1_out, or_1_out, or_2_out,
       undriven;
  wire [7:0] j_k_ff_1_q, multiplexer_1_out, multiplexer_2_out, PC_q, R0_q;

  Clock clock_1 (.out(clock_1_out));
  J_K_Flip_Flop #(.trigger("falling")) j_k_ff_1 (
    .J(1'b1), .clk(clock_1_out), .K(1'b1), .Q(j_k_ff_1_q[0]), .reset(in_5));  // open: Qn, preset, en
  J_K_Flip_Flop #(.trigger("falling")) j_k_ff_2 (
    .J(1'b1), .clk(j_k_ff_1_q[0]), .K(1'b1), .Q(j_k_ff_1_q[1]), .reset(in_5));  // open: Qn, preset, en
  J_K_Flip_Flop #(.trigger("falling")) j_k_ff_3 (
    .J(1'b1), .clk(j_k_ff_1_q[1]), .K(1'b1), .Q(j_k_ff_1_q[2]), .reset(in_5));  // open: Qn, preset, en
  J_K_Flip_Flop #(.trigger("falling")) j_k_ff_4 (
    .J(1'b1), .clk(j_k_ff_1_q[2]), .K(1'b1), .Q(j_k_ff_1_q[3]), .reset(in_5));  // open: Qn, preset, en
  J_K_Flip_Flop #(.trigger("falling")) j_k_ff_5 (
    .J(1'b1), .clk(j_k_ff_1_q[3]), .K(1'b1), .Q(j_k_ff_1_q[4]), .reset(in_5));  // open: Qn, preset, en
  J_K_Flip_Flop #(.trigger("falling")) j_k_ff_6 (
    .J(1'b1), .clk(j_k_ff_1_q[4]), .K(1'b1), .Q(j_k_ff_1_q[5]), .reset(in_5));  // open: Qn, preset, en
  J_K_Flip_Flop #(.trigger("falling")) j_k_ff_7 (
    .J(1'b1), .clk(j_k_ff_1_q[5]), .K(1'b1), .Q(j_k_ff_1_q[6]), .reset(in_5));  // open: Qn, preset, en
  J_K_Flip_Flop #(.trigger("falling")) j_k_ff_8 (
    .J(1'b1), .clk(j_k_ff_1_q[6]), .K(1'b1), .Q(j_k_ff_1_q[7]), .reset(in_5));  // open: Qn, preset, en
  Register PC (.D(j_k_ff_1_q), .Q(PC_q), .clk(clock_1_out));  // open: en, clr
  not not_1 (not_1_out, clock_1_out);
  RAM ram_1 (.addr(PC_q), .data({out_30, out_10, out_11}), .clk(not_1_out));  // open: sel, ld, clr
  Clock clock_2 (.out(clock_2_out));
  Register R0 (.D(out_9), .en(undriven), .Q(R0_q), .clk(clock_2_out));  // open: clr
  Multiplexer #(.select(2), .width(8)) multiplexer_1 (
    .in0(R0_q), .in1(out_8), .in2(out_7), .in3(out_6), .out(multiplexer_1_out), .sel(out_10));  // open: en
  Register R1 (.D(E1), .Q(out_8), .clk(clock_2_out));  // open: en, clr
  Register R2 (.D(E2), .Q(out_7), .clk(clock_2_out));  // open: en, clr
  Multiplexer #(.select(2), .width(8)) multiplexer_2 (
    .in0(R0_q), .in1(out_8), .in2(out_7), .in3(out_6), .out(multiplexer_2_out), .sel(out_11));  // open: en
  Register R3 (.D(E3), .Q(out_6), .clk(clock_2_out));  // open: en, clr
  Demultiplexer #(.select(4), .width(8)) demultiplexer_1 (
    .out0(out_13), .out1(out_14), .out2(out_16), .out3(out_17), .out4(out_18), .out5(out_20), .out6(out_21),
    .out7(out_23), .out8(out_24), .out9(out_25), .out10(out_27), .out11(out_28), .in(multiplexer_1_out),
    .sel(out_30));  // open: out12, out13, out14, out15, en
  Demultiplexer #(.select(4), .width(8)) demultiplexer_2 (
    .out0(out_32), .out1(out_34), .out2(out_35), .out3(out_36), .out4(out_37), .out5(out_38), .out6(out_40),
    .out7(out_41), .out8(out_42), .out9(out_43), .out10(out_44), .in(multiplexer_2_out), .sel(out_30));  // open: out11, out12, out13, out14, out15, en
  Comparator #(.mode("unsigned")) comparator_1 (.a(out_21), .b(out_40), .eq(comparator_1_eq));  // open: gt, lt
  Comparator #(.mode("unsigned")) comparator_2 (.a(out_23), .b(out_41), .lt(comparator_2_lt));  // open: gt, eq
  Comparator #(.mode("unsigned")) comparator_3 (.a(out_24), .b(out_42), .gt(comparator_3_gt));  // open: eq, lt
  Comparator #(.mode("unsigned")) comparator_4 (
    .a(out_25), .b(out_43), .eq(comparator_4_eq), .lt(comparator_4_lt));  // open: gt
  or or_1 (or_1_out, comparator_4_eq, comparator_4_lt);
  or or_2 (or_2_out, comparator_5_gt, comparator_5_eq);
  Comparator #(.mode("unsigned")) comparator_5 (
    .a(out_27), .b(out_44), .gt(comparator_5_gt), .eq(comparator_5_eq));  // open: lt
  assign out_12 = out_13 & out_32;  // AND_Gate and_1, 8 bits wide
  assign out_15 = out_14 | out_34;  // OR_Gate or_3, 8 bits wide
  assign out_19 = out_16 ^ out_35;  // XOR_Gate xor_1, 8 bits wide
  assign out_22 = ~out_17;  // NOT_Gate not_2, 8 bits wide
  Adder adder_1 (.a(out_18), .b(out_37), .out(out_26), .cout(adder_1_cout));  // open: cin
  Subtractor subtractor_1 (.a(out_20), .b(out_38), .out(out_29));  // open: bin, bout
  Multiplexer #(.select(4), .width(8)) multiplexer_3 (
    .in0(out_12), .in1(out_15), .in2(out_19), .in3(out_22), .in4(out_26), .in5(out_29), .in6(out_31),
    .in7(out_33), .in8(out_39), .in9(out_45), .in10(out_46), .out(out_9), .sel(out_30));  // open: in11, in12, in13, in14, in15, en
  Multiplexer #(.width(8)) multiplexer_4 (
    .in0({8{1'b0}}), .in1(8'h1), .out(out_31), .sel(comparator_1_eq));  // open: en
  Multiplexer #(.width(8)) multiplexer_5 (
    .in0({8{1'b0}}), .in1(8'h1), .out(out_33), .sel(comparator_2_lt));  // open: en
  Multiplexer #(.width(8)) multiplexer_6 (
    .in0({8{1'b0}}), .in1(8'h1), .out(out_39), .sel(comparator_3_gt));  // open: en
  Multiplexer #(.width(8)) multiplexer_7 (.in0({8{1'b0}}), .in1(8'h1), .out(out_45), .sel(or_1_out));  // open: en
  Multiplexer #(.width(8)) multiplexer_8 (.in0({8{1'b0}}), .in1(8'h1), .out(out_46), .sel(or_2_out));  // open: en

  // Notes on the sheet:
  //   1
  //   2
  //   4
  //   8
  //   16
  //   32
  //   64
  //   128
  //   Rx
  //   Ry
  //   Rx
  //   Ry
endmodule
