// Logisim project memoria.circ as structural Verilog: 1 circuit, main circuit main
module main (
  input  Teste_igualdade,
  input  clear,
  input  seletor_de_bit,
  output out_4,
  output [15:0] out_5,
  output Indica_se_terminou_a_contagem,
  output [7:0] out_7,
  output [7:0] out_8
);

  wire \_1_armazena__0_lê_out , clock_1_out, comparator_1_eq, not_1_out;
  wire [15:0] counter_1_q;

  Counter #(.width(16), .max('hffff), .ongoal("load")) counter_1 (
    .load(Teste_igualdade), .D(16'hffaf), .Q(counter_1_q), .carry(Indica_se_terminou_a_contagem),
    .clk(clock_1_out), .clr(clear));  // open: count
  Clock clock_1 (.out(clock_1_out));
  Register #(.width(1)) register_1 (.D(1'b1), .Q(out_4), .clk(Indica_se_terminou_a_contagem));  // open: en, clr
  Register register_2 (.D(counter_1_q[7:0]), .Q(out_5[7:0]), .clk(clock_1_out));  // open: en, clr
  Register register_3 (.D(counter_1_q[15:8]), .Q(out_5[15:8]), .clk(clock_1_out));  // open: en, clr
  BitSelector #(.width(16), .group(8)) bitselector_1 (.in(counter_1_q), .out(out_8), .sel(seletor_de_bit));
  Comparator #(.mode("unsigned")) comparator_1 (.a(out_8), .b(out_7), .eq(comparator_1_eq));  // open: gt, lt
  not not_1 (not_1_out, comparator_1_eq);
  not \_1_armazena__0_lê  (\_1_armazena__0_lê_out , out_4);
  LED \Entrada_e_saída_iguais  (.in(not_1_out));
  RAM #(.addrWidth(16), .bus("separate")) ram_1 (
    .addr(out_5), .din(out_8), .data(out_7), .str(\_1_armazena__0_lê_out ), .clk(clock_1_out));  // open: sel, ld, clr

  // Notes on the sheet:
  //   endereçamento
  //   entrada de dados
endmodule
